// Digital circuit random_generator.dig as structural Verilog
module random_generator (
  input  in_2,
  input  in_3,
  input  clk,
  input  [3:0] in_5,
  input  clk_2,
  output [3:0] out_1,
  output [3:0] out_7
);

  lfsr #(.applicationType("IVERILOG")) u_lfsr (.enable(in_2), .clk(clk), .reset(in_3), .data(in_5), .out(out_1));
  test #(.applicationType("IVERILOG")) u_test (.clk(clk_2), .out(out_7));
endmodule

/* Code of lfsr:
module lfsr(
    output reg[3:0] out,  // Output of the counter
    input enable,  // Enable  for counter
    input clk,  // clock input
    input reset,              // reset input
    input [3:0]data
);

wire        linear_feedback;
 
assign linear_feedback =  ! (out[2] ^ data[1]);

always @(posedge clk)
    if (reset) begin // active high reset
        out <= 4'd0 ;
    end
    else 
        if (enable) begin
            out <= {(out[1] && data[3]),
		(out[3]|| data[0]),
		(out[0] ^ data [2]),
		 linear_feedback};
        end 

endmodule // End Of Module counter
*/

/* Code of test:
module test(
    input clk,
    output reg[3:0] out
);
      reg[3:0]a;
      reg [3:0] i;

      always @(posedge clk ) begin
        for (i=0; i < 10; i=i+1) begin
           out=$urandom%9; 
        end 
      end
endmodule
*/
